# Fritzing sketch morse (saved by Fritzing 0.9.2b)
circuit board: 4.23cm x 4.23cm
breadboards: 1

parts:
  U1 = ATTINY45 [package=dip]
  R1 = Resistor [tolerance=±5% resistance=47 package=THT]
  LED1 = LED - 3mm [color="Blue (470nm)" package="3 mm [THT]"]
  Part1 = LilyPad Coin Cell Battery Holder

nets:
  N1: U1.GND, LED1.anode, Part1.-
  N2: U1.PB0(MOSI), R1.Pin_1
  N3: U1.VCC, Part1.+
  N4: R1.Pin_0, LED1.cathode
